// Logisim project hw4.circ as structural Verilog
module Processor (
  input  reset
);

  wire ALU__WIP_zero, clock_1_out, undriven, undriven_2, undriven_3;
  wire [15:0] adder_1_out, ALU__WIP_dataout, bit_extender_1_out, bit_extender_2_out, multiplexer_1_out,
       multiplexer_2_out, multiplexer_3_out, PC_q, ram_1_data, RegisterFile_out1, RegisterFile_out2,
       rom_1_data;

  Clock clock_1 (.out(clock_1_out));
  Register #(.width(16)) PC (.D(multiplexer_3_out), .Q(PC_q), .clk(clock_1_out), .clr(reset));  // open: en
  Adder #(.width(16)) adder_1 (.a(PC_q), .b(16'h4), .out(adder_1_out));  // open: cin, cout
  ROM #(.addrWidth(16), .dataWidth(16)) rom_1 (.addr(PC_q), .data(rom_1_data));  // open: sel
  Control control_1 ();
  assign bit_extender_1_out = {{10{rom_1_data[15]}}, rom_1_data[15:10]};  // Bit_Extender bit_extender_1
  assign bit_extender_2_out = {{4{1'b0}}, rom_1_data[15:4]};  // Bit_Extender bit_extender_2
  RegisterFile RegisterFile (
    .RegWrite(undriven_2), .Write_Data(multiplexer_2_out), .Read_Reg_1(rom_1_data[6:4]),
    .Read_Reg_2(rom_1_data[9:7]), .clock(clock_1_out), .reset(reset), .out1(RegisterFile_out1),
    .out2(RegisterFile_out2));  // open: Write_Reg
  Multiplexer #(.width(16), .enable("false")) multiplexer_1 (
    .in0(RegisterFile_out2), .in1(bit_extender_1_out), .out(multiplexer_1_out), .sel(undriven_3));
  ALU ALU__WIP (
    .in1___rs(RegisterFile_out1), .dataOut(ALU__WIP_dataout), .in2___rt_imm(multiplexer_1_out),
    .Zero(ALU__WIP_zero));  // open: Opcode
  Multiplexer #(.width(16)) multiplexer_2 (
    .in0(ALU__WIP_dataout), .in1(ram_1_data), .out(multiplexer_2_out));  // open: sel, en
  RAM #(.addrWidth(16), .dataWidth(16), .bus("separate")) ram_1 (
    .addr(ALU__WIP_dataout), .din(RegisterFile_out2), .data(ram_1_data), .clr(reset));  // open: str, sel, clk, ld
  Multiplexer #(.width(16), .enable("false")) multiplexer_3 (
    .in0(adder_1_out), .in1(bit_extender_2_out), .out(multiplexer_3_out), .sel(undriven));
endmodule

module RegisterFile (
  input  RegWrite,
  input  [15:0] Write_Data,
  input  [2:0] Write_Reg,
  input  [2:0] Read_Reg_1,
  input  [2:0] Read_Reg_2,
  input  clock,
  input  reset,
  output [15:0] out1,
  output [15:0] out2
);

  wire demultiplexer_1_out0, demultiplexer_1_out1, demultiplexer_1_out2, demultiplexer_1_out3,
       demultiplexer_1_out4, demultiplexer_1_out5, demultiplexer_1_out6, demultiplexer_1_out7;
  wire [15:0] Clock_Trigger_q, r0_q, r1_q, r2_q, r3_q, r4_q, r5_q, r6_q, r7_q;

  Register #(.width(16), .trigger("falling")) Clock_Trigger (
    .D(Write_Data), .Q(Clock_Trigger_q), .clk(clock), .clr(reset));  // open: en
  Demultiplexer #(.select(3)) demultiplexer_1 (
    .out0(demultiplexer_1_out0), .out1(demultiplexer_1_out1), .out2(demultiplexer_1_out2),
    .out3(demultiplexer_1_out3), .out4(demultiplexer_1_out4), .out5(demultiplexer_1_out5),
    .out6(demultiplexer_1_out6), .out7(demultiplexer_1_out7), .in(RegWrite), .sel(Write_Reg));  // open: en
  Register #(.width(16), .trigger("high")) r0 (
    .D(Clock_Trigger_q), .Q(r0_q), .clk(demultiplexer_1_out0), .clr(reset));  // open: en
  Register #(.width(16), .trigger("high")) r1 (
    .D(Clock_Trigger_q), .Q(r1_q), .clk(demultiplexer_1_out1), .clr(reset));  // open: en
  Register #(.width(16), .trigger("high")) r2 (
    .D(Clock_Trigger_q), .Q(r2_q), .clk(demultiplexer_1_out2), .clr(reset));  // open: en
  Register #(.width(16), .trigger("high")) r3 (
    .D(Clock_Trigger_q), .Q(r3_q), .clk(demultiplexer_1_out3), .clr(reset));  // open: en
  Register #(.width(16), .trigger("high")) r4 (
    .D(Clock_Trigger_q), .Q(r4_q), .clk(demultiplexer_1_out4), .clr(reset));  // open: en
  Register #(.width(16), .trigger("high")) r5 (
    .D(Clock_Trigger_q), .Q(r5_q), .clk(demultiplexer_1_out5), .clr(reset));  // open: en
  Register #(.width(16), .trigger("high")) r6 (
    .D(Clock_Trigger_q), .Q(r6_q), .clk(demultiplexer_1_out6), .clr(reset));  // open: en
  Register #(.width(16), .trigger("high")) r7 (
    .D(Clock_Trigger_q), .Q(r7_q), .clk(demultiplexer_1_out7), .clr(reset));  // open: en
  Multiplexer #(.select(3), .width(16), .enable("false")) multiplexer_1 (
    .in0(r0_q), .in1(r1_q), .in2(r2_q), .in3(r3_q), .in4(r4_q), .in5(r5_q), .in6(r6_q), .in7(r7_q),
    .out(out1), .sel(Read_Reg_1));
  Multiplexer #(.select(3), .width(16), .enable("false")) multiplexer_2 (
    .in0(r0_q), .in1(r1_q), .in2(r2_q), .in3(r3_q), .in4(r4_q), .in5(r5_q), .in6(r6_q), .in7(r7_q),
    .out(out2), .sel(Read_Reg_2));
endmodule

module ALU (
  input  [15:0] in1___rs,
  input  [15:0] in2___rt_imm,
  input  [3:0] Opcode,
  output Zero,
  output [15:0] dataOut
);

  wire comparator_1_eq, comparator_1_lt;
  wire [3:0] bit_extender_1_out, bit_extender_2_out;
  wire [15:0] adder_1_out, bit_extender_3_out, bit_extender_4_out, not_1_out, shifter_1_out, shifter_2_out,
       subtractor_1_out, xor_1_out;

  assign xor_1_out = in1___rs ^ in2___rt_imm;  // XOR_Gate xor_1, 16 bits wide
  assign not_1_out = ~in1___rs;  // NOT_Gate not_1, 16 bits wide
  Adder #(.width(16)) adder_1 (.a(in1___rs), .b(in2___rt_imm), .out(adder_1_out));  // open: cin, cout
  Subtractor #(.width(16)) subtractor_1 (.a(in1___rs), .b(in2___rt_imm), .out(subtractor_1_out));  // open: bin, bout
  Bit_Extender #(.in_width(16), .out_width(4)) bit_extender_1 (.in(in2___rt_imm), .out(bit_extender_1_out));
  Bit_Extender #(.in_width(16), .out_width(4)) bit_extender_2 (.in(in2___rt_imm), .out(bit_extender_2_out));
  Comparator #(.width(16)) comparator_1 (
    .a(in1___rs), .b(in2___rt_imm), .eq(comparator_1_eq), .lt(comparator_1_lt));  // open: gt
  Shifter #(.width(16), .shift("ar")) shifter_1 (.in(in1___rs), .\dist (bit_extender_1_out), .out(shifter_1_out));
  Shifter #(.width(16)) shifter_2 (.in(in1___rs), .\dist (bit_extender_2_out), .out(shifter_2_out));
  assign bit_extender_3_out = {{15{1'b0}}, comparator_1_eq};  // Bit_Extender bit_extender_3
  assign bit_extender_4_out = {{15{1'b0}}, comparator_1_lt};  // Bit_Extender bit_extender_4
  Multiplexer #(.select(4), .width(16)) multiplexer_1 (
    .in0(not_1_out), .in1(xor_1_out), .in2(adder_1_out), .in3(adder_1_out), .in4(subtractor_1_out),
    .in5(shifter_1_out), .in6(shifter_2_out), .in7({16{1'b0}}), .in8({16{1'b0}}), .in9({16{1'b0}}),
    .in10({16{1'b0}}), .in11({16{1'b0}}), .in12(bit_extender_3_out), .in13(bit_extender_4_out),
    .in14({16{1'b0}}), .in15(in1___rs), .out(dataOut), .sel(Opcode));  // open: en
  nor Z (Zero, dataOut[0], dataOut[1], dataOut[2], dataOut[3], dataOut[4], dataOut[5], dataOut[6], dataOut[7], dataOut[8], dataOut[9], dataOut[10], dataOut[11], dataOut[12], dataOut[13], dataOut[14], dataOut[15]);
endmodule
